# Fritzing sketch Pico-ISA-Breadboard (saved by Fritzing 0.9.9b)
breadboards: 2
perfboards: 1

parts:
  U1 = Raspberry Pi Pico [part_number="Pi Pico"]
  U2 = IC, DIP package, 20 pins [chip_label=74LVC245 part_number=74LVC245A]
  D1 = Diode [package=diode-1n4148]
  J1 = female pin header, 8 pins [form="♀ (female)"]
  J2 = female pin header, 5 pins [form="♀ (female)"]
  U3 = IC, DIP package, 20 pins [chip_label=74HCT244 part_number=SN74HCT244]
  J5 = female pin header, 4 pins [form="♀ (female)"]
  J4 = female pin header, 8 pins [form="♀ (female)"]  # not connected
  J3 = female pin header, 8 pins [form="♀ (female)"]
  J6 = female pin header, 4 pins [form="♀ (female)"]
  R1 = Resistor [tolerance=±1% power=0.25 resistance=5.1k package=THT]
  U4 = IC, DIP package, 20 pins [chip_label=74HCT244 part_number=SN74HCT244]
  R2 = Resistor [tolerance=±1% power=0.25 resistance=5.1k package=THT]
  R3 = Resistor [tolerance=±1% power=0.25 resistance=5.1k package=THT]
  R4 = Resistor [tolerance=±1% power=0.25 resistance=5.1k package=THT]
  R7 = Resistor [tolerance=±1% power=0.25 resistance=10k package=THT]
  C2 = Capacitor [package=cap-pth-small2]
  R8 = Resistor [tolerance=±1% power=0.25 resistance=1k package=THT]
  R9 = Resistor [tolerance=±1% power=0.25 resistance=2k package=THT]
  C3 = Capacitor [package=cap-pth-small2]
  C4 = Capacitor [package=cap-pth-small2]
  C5 = Capacitor [package=cap-pth-small2]
  C6 = Capacitor [package=cap-pth-small2]
  C7 = Capacitor [package=cap-pth-small2]
  C8 = Capacitor [package=cap-pth-small2]
  C9 = Capacitor [package=cap-pth-small2]
  C10 = Capacitor [package=cap-pth-small2]
  C11 = Capacitor [package=cap-pth-small2]
  C12 = Capacitor [package=cap-pth-small2]
  U5 = IC, DIP package, 16 pins [chip_label=74HC595]

nets (from the breadboard view):
  N1: U1.pin_1, U2.pin18
  N2: U1.pin_2, U2.pin17
  N3: U1.pin_3, U1.pin_8, U1.pin_13, U1.pin_18, U1.pin_23, U1.pin_28, U1.pin_33, U1.pin_38, U1.pin_42
  N4: U1.pin_4, U2.pin16
  N5: U1.pin_5, U2.pin15
  N6: U1.pin_6, U2.pin14
  N7: U1.pin_7, U2.pin13
  N8: U1.pin_9, U2.pin12
  N9: U1.pin_10, U2.pin11
  N10: U1.pin_11, U4.pin17
  N11: U1.pin_12, U4.pin15
  N12: U1.pin_14, U4.pin13
  N13: U1.pin_15, U4.pin11
  N14: U1.pin_16, U4.pin8
  N15: U1.pin_17, U4.pin6
  N16: U1.pin_19, U4.pin4
  N17: U1.pin_20, U4.pin2
  N18: U1.pin_21, U2.pin19, U3.pin1, U4.pin1, U4.pin19, R7.Pin_0, U5.pin13
  N19: U1.pin_22, R8.Pin_1, R9.Pin_0
  N20: U1.pin_24, U3.pin8
  N21: U1.pin_25, U3.pin6
  N22: U1.pin_26, U3.pin4
  N23: U1.pin_27, U3.pin2
  N24: U1.pin_29, U2.pin1, U3.pin17
  N25: U1.pin_32, U5.pin11, U5.pin12
  N26: U1.pin_39, U2.pin10, J2.pin5, U3.pin19, J6.pin1, C2.1, C3.1, C4.1, C6.1, C7.1, C8.1, U5.pin8
  N27: U2.pin2, J1.pin1
  N28: U2.pin3, J1.pin2
  N29: U2.pin4, J1.pin3
  N30: U2.pin5, J1.pin4
  N31: U2.pin6, J1.pin5
  N32: U2.pin7, J1.pin6
  N33: U2.pin8, J1.pin7
  N34: U2.pin9, J1.pin8
  N35: U2.pin20, R7.Pin_1, C5.2, C9.2, C10.2, C11.2, C12.2, U5.pin10
  N36: D1.A, U3.pin20, J6.pin4, R1.Pin_1, R2.Pin_1, R3.Pin_1, R4.Pin_1, C2.2, C3.2, C4.2, C6.2, C7.2
  N37: J2.pin1, U3.pin18, R4.Pin_0
  N38: J2.pin2, U3.pin16, R3.Pin_0
  N39: J2.pin3, U3.pin14, R2.Pin_0
  N40: J2.pin4, U3.pin12, R1.Pin_0
  N41: U3.pin3, J6.pin2
  N42: U3.pin10, U4.pin10, C5.1, C8.2, C9.1, C10.1, C11.1, C12.1
  N43: J5.pin1, U5.pin15
  N44: J5.pin2, U5.pin1
  N45: J5.pin3, U5.pin2
  N46: J5.pin4, U5.pin3
  N47: J3.pin1, U4.pin3
  N48: J3.pin2, U4.pin5
  N49: J3.pin3, U4.pin7
  N50: J3.pin4, U4.pin9
  N51: J3.pin5, U4.pin12
  N52: J3.pin6, U4.pin14
  N53: J3.pin7, U4.pin16
  N54: J3.pin8, U4.pin18
  N55: J6.pin3, R8.Pin_0

notes:
  Data7-0
  MEMW#
  MEMR#
  IOW#
  IOR#
  Address 19-0
  Data Bus Dir:
  0 Write Pico -> ISA
  1 Read ISA -> Pico
  5V+
  N.C.
  RESET
  Gnd

custom parts:
  Raspberry Pi Pico: Raspberry Pi Pico. Based around the RP2040 microcontroller the Pico is a low cost microcontroller device bringing Raspberry Pi quality, cost, and easy of use to the microcontroller space. Jan 2021, Split part in to two versions: tht (this one) and SMD. This one will drill holes for a .1 in header in pcb to allow plugging in the module as well as providing pads to solder the module to the top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
