# Fritzing sketch Pico-ISA-Protoboard (saved by Fritzing 0.9.9b)
perfboards: 1

parts:
  U1 = Raspberry Pi Pico
  U2 = IC, DIP package, 20 pins [chip_label=74LVC245]
  U6 = IC, DIP package, 20 pins [chip_label=74HCT244]
  R1 = Resistor [tolerance=±1% power=0.25 resistance=5.1k package=THT]
  R2 = Resistor [tolerance=±1% power=0.25 resistance=5.1k package=THT]
  R3 = Resistor [tolerance=±1% power=0.25 resistance=5.1k package=THT]
  R4 = Resistor [tolerance=±1% power=0.25 resistance=5.1k package=THT]
  R8 = Resistor [tolerance=±1% power=0.25 resistance=2k package=THT]
  R9 = Resistor [tolerance=±1% power=0.25 resistance=1k package=THT]
  GND = female pin header, 1 pin [form="♀ (female)"]
  Reset = female pin header, 1 pin [form="♀ (female)"]
  +5V = female pin header, 1 pin [form="♀ (female)"]
  IRQ2 = female pin header, 1 pin [form="♀ (female)"]
  -5V = female pin header, 1 pin [form="♀ (female)"]  # not connected
  DRQ2 = female pin header, 1 pin [form="♀ (female)"]  # not connected
  -12V = female pin header, 1 pin [form="♀ (female)"]  # not connected
  CARDSEL = female pin header, 1 pin [form="♀ (female)"]  # not connected
  +12V = female pin header, 1 pin [form="♀ (female)"]  # not connected
  IOW# = female pin header, 1 pin [form="♀ (female)"]
  GND_2 = female pin header, 1 pin [form="♀ (female)"]
  IOR# = female pin header, 1 pin [form="♀ (female)"]
  MEMW# = female pin header, 1 pin [form="♀ (female)"]
  MEMR# = female pin header, 1 pin [form="♀ (female)"]
  DRQ3 = female pin header, 1 pin [form="♀ (female)"]  # not connected
  DACK3# = female pin header, 1 pin [form="♀ (female)"]  # not connected
  DACK1# = female pin header, 1 pin [form="♀ (female)"]  # not connected
  IRQ7 = female pin header, 1 pin [form="♀ (female)"]  # not connected
  IRQ5 = female pin header, 1 pin [form="♀ (female)"]  # not connected
  ALE = female pin header, 1 pin [form="♀ (female)"]  # not connected
  DACK0# = female pin header, 1 pin [form="♀ (female)"]  # not connected
  IRQ6 = female pin header, 1 pin [form="♀ (female)"]  # not connected
  DRQ1 = female pin header, 1 pin [form="♀ (female)"]  # not connected
  TC = female pin header, 1 pin [form="♀ (female)"]  # not connected
  +5V_2 = female pin header, 1 pin [form="♀ (female)"]
  IRQ3 = female pin header, 1 pin [form="♀ (female)"]  # not connected
  GND_3 = female pin header, 1 pin [form="♀ (female)"]
  CLK = female pin header, 1 pin [form="♀ (female)"]  # not connected
  IRQ4 = female pin header, 1 pin [form="♀ (female)"]  # not connected
  OSC = female pin header, 1 pin [form="♀ (female)"]  # not connected
  DACK2# = female pin header, 1 pin [form="♀ (female)"]  # not connected
  IOCHK = female pin header, 1 pin [form="♀ (female)"]  # not connected
  A13 = female pin header, 1 pin [form="♀ (female)"]
  A2 = female pin header, 1 pin [form="♀ (female)"]
  A5 = female pin header, 1 pin [form="♀ (female)"]
  D5 = female pin header, 1 pin [form="♀ (female)"]
  D3 = female pin header, 1 pin [form="♀ (female)"]
  A8 = female pin header, 1 pin [form="♀ (female)"]
  A9 = female pin header, 1 pin [form="♀ (female)"]
  AEN = female pin header, 1 pin [form="♀ (female)"]
  D6 = female pin header, 1 pin [form="♀ (female)"]
  A7 = female pin header, 1 pin [form="♀ (female)"]
  A0 = female pin header, 1 pin [form="♀ (female)"]
  D4 = female pin header, 1 pin [form="♀ (female)"]
  D0 = female pin header, 1 pin [form="♀ (female)"]
  A15 = female pin header, 1 pin [form="♀ (female)"]
  A18 = female pin header, 1 pin [form="♀ (female)"]
  A1 = female pin header, 1 pin [form="♀ (female)"]
  A3 = female pin header, 1 pin [form="♀ (female)"]
  A11 = female pin header, 1 pin [form="♀ (female)"]
  A6 = female pin header, 1 pin [form="♀ (female)"]
  A17 = female pin header, 1 pin [form="♀ (female)"]
  A14 = female pin header, 1 pin [form="♀ (female)"]
  D1 = female pin header, 1 pin [form="♀ (female)"]
  A10 = female pin header, 1 pin [form="♀ (female)"]
  A19 = female pin header, 1 pin [form="♀ (female)"]
  A12 = female pin header, 1 pin [form="♀ (female)"]
  IORDY = female pin header, 1 pin [form="♀ (female)"]  # not connected
  A16 = female pin header, 1 pin [form="♀ (female)"]
  D7 = female pin header, 1 pin [form="♀ (female)"]
  A4 = female pin header, 1 pin [form="♀ (female)"]
  D2 = female pin header, 1 pin [form="♀ (female)"]
  D8 = Diode [package=diode-hv]
  R10 = Resistor [tolerance=±1% power=0.25 resistance=10k package=THT]
  U4 = IC, DIP package, 16 pins [chip_label=74HC595]
  U3 = IC, DIP package, 20 pins [chip_label=74HCT244]
  U5 = IC, DIP package, 16 pins [chip_label=74HC595]

nets:
  N1: U1.pin_1, U2.pin11
  N2: U1.pin_2, U2.pin12
  GND: U1.pin_3, U1.pin_8, U1.pin_13, U1.pin_18, U1.pin_23, U1.pin_28, U1.pin_33, U1.pin_38, U2.pin10, U6.pin10, U6.pin11, U6.pin13, U6.pin15, U6.pin19, R8.Pin_0, GND.pin1, GND_2.pin1, GND_3.pin1, AEN.pin1, U4.pin8, U3.pin10, U5.pin8
  N3: U1.pin_4, U2.pin13
  N4: U1.pin_5, U2.pin14
  N5: U1.pin_6, U2.pin15
  N6: U1.pin_7, U2.pin16
  N7: U1.pin_9, U2.pin17
  N8: U1.pin_10, U2.pin18
  N9: U1.pin_11, U3.pin11
  N10: U1.pin_12, U3.pin8
  N11: U1.pin_14, U3.pin13
  N12: U1.pin_15, U3.pin6
  N13: U1.pin_16, U3.pin15
  N14: U1.pin_17, U3.pin4
  N15: U1.pin_19, U3.pin17
  N16: U1.pin_20, U3.pin2
  N17: U1.pin_21, U5.pin14
  N18: U1.pin_22, U4.pin11, U4.pin12, U5.pin11, U5.pin12
  N19: U1.pin_24, U6.pin8
  N20: U1.pin_25, U6.pin6
  N21: U1.pin_26, U6.pin4
  N22: U1.pin_27, U6.pin2
  N23: U1.pin_29, U2.pin19, U6.pin1, U6.pin17, R10.Pin_0, U4.pin13, U3.pin1, U3.pin19, U5.pin13
  N24: U1.pin_32, U2.pin1
  N25: U1.pin_34, R8.Pin_1, R9.Pin_0
  3.3V: U1.pin_36, U2.pin20, R10.Pin_1, U4.pin10, U4.pin16, U5.pin10, U5.pin16
  N26: U1.pin_39, D8.C
  N27: U2.pin2, D0.pin1
  N28: U2.pin3, D1.pin1
  N29: U2.pin4, D2.pin1
  N30: U2.pin5, D3.pin1
  N31: U2.pin6, D4.pin1
  N32: U2.pin7, D5.pin1
  N33: U2.pin8, D6.pin1
  N34: U2.pin9, D7.pin1
  N35: U6.pin3, Reset.pin1
  N36: U6.pin12, R4.Pin_0, IOR#.pin1
  N37: U6.pin14, R3.Pin_0, IOW#.pin1
  N38: U6.pin16, R2.Pin_0, MEMR#.pin1
  N39: U6.pin18, R1.Pin_0, MEMW#.pin1
  5V: U6.pin20, R1.Pin_1, R2.Pin_1, R3.Pin_1, R4.Pin_1, +5V.pin1, +5V_2.pin1, D8.A, U3.pin20
  N40: R9.Pin_1, IRQ2.pin1
  N41: A13.pin1, U5.pin5
  N42: A2.pin1, U3.pin7
  N43: A5.pin1, U3.pin16
  N44: A8.pin1, U5.pin15
  N45: A9.pin1, U5.pin1
  N46: A7.pin1, U3.pin18
  N47: A0.pin1, U3.pin9
  N48: A15.pin1, U5.pin7
  N49: A18.pin1, U4.pin2
  N50: A1.pin1, U3.pin12
  N51: A3.pin1, U3.pin14
  N52: A11.pin1, U5.pin3
  N53: A6.pin1, U3.pin3
  N54: A17.pin1, U4.pin1
  N55: A14.pin1, U5.pin6
  N56: A10.pin1, U5.pin2
  N57: A19.pin1, U4.pin3
  N58: A12.pin1, U5.pin4
  N59: A16.pin1, U4.pin15
  N60: A4.pin1, U3.pin5
  N61: U4.pin14, U5.pin9

notes:
  Data Bus Dir:
  0 Write ISA -> Pico
  1 Read Pico -> ISA
  Data bits are reversed
  GP0 - D7, GP7 - D0

custom parts:
  Raspberry Pi Pico: Raspberry Pi Pico. Based around the RP2040 microcontroller the Pico is a low cost microcontroller device bringing Raspberry Pi quality, cost, and easy of use to the microcontroller space. Jan 2021, Split part in to two versions: tht (this one) and SMD. This one will drill holes for a .1 in header in pcb to allow plugging in the module as well as providing pads to solder the module to the top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
